# Fritzing sketch PP2SFC (saved by Fritzing 0.9.3b)
breadboards: 2

parts:
  X2 = shrouded pin header, 16 pins [form="♂ (shrouded male)"]
  Arduino_Nano = Arduino Nano (Rev3.0)
  IC2 = IC, DIP package, 16 pins [chip_label=4021]
  IC1 = IC, DIP package, 16 pins [chip_label=4021]
  R52 = Resistor [tolerance=±5% resistance=56k package=THT]
  R55 = Resistor [tolerance=±5% resistance=56k package=THT]
  R56 = Resistor [tolerance=±5% resistance=56k package=THT]
  J8 = female pin header, 6 pins [form="♀ (female)"]
  R60 = Resistor [tolerance=±5% resistance=56k package=THT]
  R61 = Resistor [tolerance=±5% resistance=56k package=THT]
  R62 = Resistor [tolerance=±5% resistance=56k package=THT]
  R63 = Resistor [tolerance=±5% resistance=56k package=THT]
  R64 = Resistor [tolerance=±5% resistance=56k package=THT]
  R65 = Resistor [tolerance=±5% resistance=56k package=THT]
  R66 = Resistor [tolerance=±5% resistance=56k package=THT]
  R67 = Resistor [tolerance=±5% resistance=56k package=THT]
  R68 = Resistor [tolerance=±5% resistance=56k package=THT]
  R69 = Resistor [tolerance=±5% resistance=56k package=THT]
  R70 = Resistor [tolerance=±5% resistance=56k package=THT]
  D1 = Rectifier Diode [part_number=1N4001 package="300 mil [THT]"]
  R74 = Resistor [tolerance=±5% resistance=56k package=THT]
  R75 = Resistor [tolerance=±5% resistance=56k package=THT]
  X1 = DB9 Connector [package=db9]
  X3 = DB9 Connector [package=db9]
  X5 = DB9 Connector [package=db9]
  X7 = DB9 Connector [package=db9]
  X4 = shrouded pin header, 16 pins [form="♂ (shrouded male)"]
  X6 = shrouded pin header, 8 pins [form="♂ (shrouded male)"]
  X8 = Camdenboss CTB0158-7 [part_number=CTB0158-7 package=THT]
  J9 = female pin header, 5 pins [form="♀ (female)"]

nets:
  N1: X2.pin1, Arduino_Nano.5V, J8.pin5
  N2: X2.pin2, Arduino_Nano.D13/SCK, J8.pin4
  N3: X2.pin3, Arduino_Nano.D8, J8.pin3
  N4: X2.pin4, Arduino_Nano.GND, IC2.pin8, IC2.pin11, IC1.pin8, J8.pin6, X1.9, J9.pin5
  N5: X2.pin7, Arduino_Nano.D11/MOSI, J8.pin1
  N6: Arduino_Nano.D2, IC2.pin1, R74.Pin_0
  N7: Arduino_Nano.D3, IC1.pin4, R55.Pin_0
  N8: Arduino_Nano.D4, IC1.pin1, R75.Pin_0
  N9: Arduino_Nano.D5, IC1.pin5, R56.Pin_0
  N10: Arduino_Nano.D6, IC1.pin6, R66.Pin_0
  N11: Arduino_Nano.D7, Arduino_Nano.D10
  N12: Arduino_Nano.D9, IC1.pin7, R65.Pin_0
  N13: Arduino_Nano.D12/MISO, J8.pin2
  N14: Arduino_Nano.A5, IC2.pin15, R52.Pin_1
  N15: Arduino_Nano.A4, IC2.pin14, R60.Pin_1
  N16: Arduino_Nano.A3, IC2.pin13, R61.Pin_1
  N17: Arduino_Nano.A2, IC1.pin15, R62.Pin_1
  N18: Arduino_Nano.A1, IC1.pin14, R63.Pin_1
  N19: Arduino_Nano.A0, IC1.pin13, R64.Pin_1
  N20: IC2.pin3, IC1.pin11
  N21: IC2.pin4, R69.Pin_0
  N22: IC2.pin5, R68.Pin_0
  N23: IC2.pin6, R70.Pin_0
  N24: IC2.pin7, R67.Pin_0
  N25: IC2.pin9, IC1.pin9, X1.3, J9.pin2
  N26: IC2.pin10, IC1.pin10, X1.4, J9.pin1
  N27: IC2.pin16, IC1.pin16, R52.Pin_0, R55.Pin_1, R56.Pin_1, R60.Pin_0, R61.Pin_0, R62.Pin_0, R63.Pin_0, R64.Pin_0, R65.Pin_1, R66.Pin_1, R67.Pin_1, R68.Pin_1, R69.Pin_1, R70.Pin_1, D1.cathode, R74.Pin_1, R75.Pin_1
  N28: IC1.pin3, X1.2, J9.pin3
  N29: D1.anode, X1.6, J9.pin4
  N30: X3.2, X4.pin13
  N31: X3.3, X4.pin12
  N32: X3.4, X4.pin14
  N33: X3.6, X4.pin15
  N34: X3.9, X4.pin1
  N35: X5.2, X6.pin4
  N36: X5.3, X6.pin3
  N37: X5.4, X6.pin2
  N38: X5.6, X6.pin5
  N39: X5.9, X6.pin1
  N40: X7.2, X8.pin4
  N41: X7.3, X8.pin3
  N42: X7.4, X8.pin2
  N43: X7.6, X8.pin1
  N44: X7.9, X8.pin7

notes:
  X2: Precision Pro DB15 Connector
  1. Vcc (5V)
  2. SCK -> D13
  3. Trigger -> D8
  4. GND
  5. NC
  6. NC
  7. Data (MOSI) -> D11
  8. NC
  9. NC
  10. NC
  11. NC
  12. NC
  13. NC
  14. NC
  15. NC
  4021
  PI1-9は56kΩの抵抗でプルアップ
  1. PI8 (FC A/SFC B : A Button)
  2. Q6
  3. Q8 DATA (FC OUT)
  4. PI4 (Up)
  5. PI3 (Down)
  6. PI2 (Right)
  7. PI1 (Left)
  8. GND
  9. P/S
  10. Clock
  11. Serial In
  12. Q7
  13. PI5 (Start : R)
  14. PI6 (Select : L)
  15. PI7 (FC B/SFC Y : X Button)
  16. VCC
  X1: FC Compatible
  1. NC
  2. OUT (赤)
  3. P/S (LATCH) (黄色)
  4. CLK (オレンジ)
  5. NC
  6. 5V (茶)
  7. NC
  8. NC
  9. GND (黒)
  Arduino 接続ピン
  D2 - IC2 1: A Button
  D3 - IC1 4: Up Key
  D4 - IC1 1: B Button
  D5 - IC1 5: Down Key
  D6 - IC1 6: Left Key
  D7 - D10: Clear SPI Register
  D8 - X2 3: Trigger
  D9 - IC1 7: Right Key
  D10: SS
  D11: MOSI - X2 7: Data
  D12 NC
  X4: Family Computer Extension
  1. GND
  2-8 NC
  9-11 NC
  12. P/S
  13. DATA
  14. CLK
  15. VCC
  X6: NES (New Famicom)
  1. GND
  2. CLK
  3. P/S
  4. DATA
  5. VCC
  6. NC
  7. NC
  X8: SNES (Super Famicom)
  1. VCC
  2. CLK
  3. P/S
  4. OUT
  5. NC
  6. NC
  7. GND
  Arduino 接続ピン
  D13: SCK - X2 2: Clock
  A0 - IC1 13: Start Button
  A1 - IC1 14: Select Button
  A2 - IC1 15: Y Button
  A3 - IC2 13: R Button
  A4 - IC2 14: L Button
  A5 - IC2 15: X Button
  A6 NC
  A7 NC
