# Fritzing sketch precision_spi_sfc (saved by Fritzing 0.9.3b)
breadboards: 2

parts:
  パーツ1 = Arduino Nano (Rev3.0)
  J5 = shrouded pin header, 16 pins [form="♂ (shrouded male)"]
  R2 = Resistor [tolerance=±5% resistance=1k package=THT]
  J6 = female pin header, 5 pins [form="♀ (female)"]
  R6 = Resistor [tolerance=±5% resistance=3.3k package=THT]
  J7 = female pin header, 5 pins [form="♀ (female)"]
  X1 = DB9 Connector [package=db9]  # not connected
  R17 = Resistor [tolerance=±5% resistance=3.3k package=THT]
  IC1 = IC, DIP package, 16 pins [chip_label=4021]
  R19 = Resistor [tolerance=±5% resistance=1k package=THT]
  R20 = Resistor [tolerance=±5% resistance=1k package=THT]
  R21 = Resistor [tolerance=±5% resistance=1k package=THT]
  R22 = Resistor [tolerance=±5% resistance=1k package=THT]
  R26 = Resistor [tolerance=±5% resistance=1k package=THT]
  R27 = Resistor [tolerance=±5% resistance=1k package=THT]
  R28 = Resistor [tolerance=±5% resistance=1k package=THT]
  R29 = Resistor [tolerance=±5% resistance=1k package=THT]
  R30 = Resistor [tolerance=±5% resistance=1k package=THT]
  IC2 = IC, DIP package, 16 pins [chip_label=4021]
  R32 = Resistor [tolerance=±5% resistance=56k package=THT]
  R33 = Resistor [tolerance=±5% resistance=56k package=THT]
  R34 = Resistor [tolerance=±5% resistance=56k package=THT]
  R35 = Resistor [tolerance=±5% resistance=56k package=THT]
  R36 = Resistor [tolerance=±5% resistance=56k package=THT]
  R37 = Resistor [tolerance=±5% resistance=56k package=THT]
  R38 = Resistor [tolerance=±5% resistance=56k package=THT]
  R39 = Resistor [tolerance=±5% resistance=56k package=THT]

nets:
  N1: パーツ1.GND, J6.pin2, IC2.pin8, IC2.pin11
  N2: パーツ1.D2, J5.pin2, J7.pin4, R22.Pin_0
  N3: パーツ1.D3, IC2.pin15, R37.Pin_1
  N4: パーツ1.D4, IC1.pin6, R28.Pin_0
  N5: パーツ1.D5, IC1.pin5, R27.Pin_0
  N6: パーツ1.D6, IC1.pin4, R26.Pin_0
  N7: パーツ1.D7, パーツ1.D10
  N8: パーツ1.D8, IC2.pin14, R38.Pin_1
  N9: パーツ1.D9, IC1.pin7, R29.Pin_0
  N10: パーツ1.D11/MOSI, J5.pin7, R2.Pin_0, J7.pin5
  N11: パーツ1.5V, J6.pin1, R6.Pin_0, R17.Pin_0, IC1.pin16, R19.Pin_0, R20.Pin_0, R21.Pin_0, IC2.pin16, R32.Pin_1, R33.Pin_1, R34.Pin_1, R36.Pin_1, R37.Pin_0, R38.Pin_0, R39.Pin_0
  N12: パーツ1.A5, IC2.pin13, R39.Pin_1
  N13: パーツ1.A4, IC2.pin1, R36.Pin_0
  N14: パーツ1.A3, IC1.pin13, R20.Pin_1
  N15: パーツ1.A2, IC1.pin14, R19.Pin_1
  N16: パーツ1.A1, IC1.pin15, R21.Pin_1
  N17: パーツ1.A0, IC1.pin1, R30.Pin_0
  N18: パーツ1.D13/SCK, J5.pin3, J7.pin3
  N19: J5.pin1, R2.Pin_1, J7.pin1, R22.Pin_1, R26.Pin_1, R27.Pin_1, R28.Pin_1, R29.Pin_1, R30.Pin_1
  N20: J5.pin4, J7.pin2, IC1.pin8
  N21: J6.pin3, IC1.pin3
  N22: J6.pin4, R6.Pin_1, IC1.pin9, IC2.pin9
  N23: J6.pin5, R17.Pin_1, IC1.pin10, IC2.pin10
  N24: IC1.pin11, IC2.pin3
  N25: IC2.pin4, R33.Pin_0
  N26: IC2.pin5, R34.Pin_0
  N27: IC2.pin6, R35.Pin_0
  N28: IC2.pin7, R32.Pin_0

notes:
  Precision Pro
  1. Vcc (5V)
  2. SCK
  3. Trigger
  4. GND
  5. NC
  6. NC
  7. Data (MOSI)
  8. NC
  9. NC
  10. NC
  11. NC
  12. NC
  13. NC
  14. NC
  15. NC
  4021
  1. PI8 (A=B/B Button)
  2. Q6
  3. Q8 DATA
  4. PI4 (Up)
  5. PI3 (Down)
  6. PI2 (Right)
  7. PI1 (Left)
  8. GND
  9. P/S
  10. Clock
  11. Serial In
  12. Q7
  13. PI5 (Start/R)
  14. PI6 (Select/L)
  15. PI7 (B=Y/X Button)
  16. VCC
  NES Compatible
  1. OUT
  2. P/S (LATCH)
  3. CLK
  4. GND
  5. 5V
  プルアップ
  CLK,P/Sを3.6k
  FC各ボタンは56k
  Precision Pro Connector
  1. MOSI -- 7 -> D11
  2. Trigger -- 3 -> D8
  3. SCK -- 2 -> D13
  4. GND -- 4
  5. 5V -- 1
  D7 -> D10 SS
